# Fritzing sketch Verdrahtung (saved by Fritzing 0.9.6b)

parts:
  U2 = WS2812 RGB LED strip
  J1 = Power Jack [package=power_jack_smd]
  L-Boost = Pushbutton [package="[THT]"]
  R-Start/Hit = Buzzer 12mm [package=buzzer-12mm]
  U1 = ESP32-38PinWide [part_number=ESP32-38PinWide]
  L-Start/Hit = Buzzer 12mm [package=buzzer-12mm]
  R-Boost = Pushbutton [package="[THT]"]
  J2 = Piezo Speaker

nets:
  GND: U2.GND, J1.GND, U1.GPIO11
  VCC: U2.VCC, J1.PWR, U1.VIN
  N1: U2.DIN, U1.GPIO21
  N2: L-Boost.Pin_1, L-Boost.Pin_2, R-Start/Hit.1, U1.GND, L-Start/Hit.1, R-Boost.Pin_1, R-Boost.Pin_2, J2.pin1
  N3: L-Boost.Pin_3, U1.GPIO23
  N4: R-Start/Hit.2, U1.GPIO19
  N5: U1.GPIO35, L-Start/Hit.2
  N6: U1.GPIO32, J2.pin2
  N7: U1.GPIO18, R-Boost.Pin_3, R-Boost.Pin_4

custom parts:
  WS2812 RGB LED strip: WS2812 strip
  ESP32-38PinWide: Generic 38-Pin ESP32 with wide format (only access to one side of pins on a breadboard) based on Stephen Lilley's HiLetgo ESP-WROOM-32 ESP32 ESP-32S Development Board.
